# Fritzing sketch board (saved by Fritzing 0.8.5b)
circuit board: 5cm x 5cm
breadboards: 1

parts:
  U2 = 74HC595 [package="DIP16 [THT]"]
  U3 = 74HC595 [package="DIP16 [THT]"]
  U4 = ATTINY45 [package=dip]
  7-Segment = 7-SEGMENT-DISPLAY-1_-RED [package=7-segment-1_pth]
  7-Segment_2 = 7-SEGMENT-DISPLAY-1_-RED [package=7-segment-1_pth]
  R1 = Resistor [tolerance=±5% resistance=220 package=THT]
  R2 = Resistor [tolerance=±5% resistance=220 package=THT]
  Enable_--> = Toggle Switch [package=THT]
  TMP36 = LM35 Temperature Sensor [package="TO92 [THT]"]
  VCC = Battery block 9V

nets:
  N1: U2.Q1, 7-Segment.C
  N2: U2.Q2, 7-Segment.D
  N3: U2.Q3, 7-Segment.E
  N4: U2.Q4, 7-Segment.B
  N5: U2.Q5, 7-Segment.A
  N6: U2.Q6, 7-Segment.F
  N7: U2.Q7, 7-Segment.G
  GND: U2.GND, U2.OE, U3.GND, U3.OE, U4.GND, TMP36.GND, VCC.-
  N8: U2.Q7', U3.DS
  VCC: U2.MR, U2.VCC, U3.MR, U3.VCC, U4.VCC, R1.Pin_0, R2.Pin_0, Enable_-->.COM, TMP36.+Vs
  N9: U2.SH_CP, U3.SH_CP, U4.PB4(ADC2)
  N10: U2.ST_CP, U3.ST_CP, U4.PB1(MISO)
  N11: U2.DS, U4.PB3(ADC3)
  N12: U3.Q1, 7-Segment_2.C
  N13: U3.Q2, 7-Segment_2.D
  N14: U3.Q3, 7-Segment_2.E
  N15: U3.Q4, 7-Segment_2.B
  N16: U3.Q5, 7-Segment_2.A
  N17: U3.Q6, 7-Segment_2.F
  N18: U3.Q7, 7-Segment_2.G
  N19: U4.PB2(SCK_ADC1), TMP36.Vout
  N20: 7-Segment.G1, 7-Segment.DP, 7-Segment.G2, R2.Pin_1
  N21: 7-Segment_2.G1, 7-Segment_2.DP, 7-Segment_2.G2, R1.Pin_1
  N22: Enable_-->.L1, VCC.+

notes:
  Temperature Sensor Board
  www.alexdaley.co
  v1 - 3/14/14
